# Fritzing sketch QuanTrac (saved by Fritzing 0.9.3b)
circuit board: 8.46667cm x 5.64444cm

parts:
  YL-83_-_Control_Board1 = YL-83 Rain Sensor - Control Board
  YL-83_-_Detection_Board1 = YL-83 Rain Sensor - Detection Board
  SHT3x2 = SHT3x
  U3 = ESP32-38PinWide [part_number=ESP32-38PinWide]
  Part2 = BH1750
  J1 = female pin header, 3 pins [form="♀ (female)"]
  J2 = female pin header, 3 pins [form="♀ (female)"]

nets:
  VCC: YL-83_-_Control_Board1.VCC, SHT3x2.VIN, U3.3.3, Part2.VCC, J1.pin1, J2.pin1
  N1: YL-83_-_Control_Board1.GND, U3.GPIO11, J1.pin2, J2.pin2
  N2: YL-83_-_Control_Board1.DO, U3.GPIO33
  N3: YL-83_-_Control_Board1.POS, YL-83_-_Detection_Board1.POS
  N4: YL-83_-_Control_Board1.NEG, YL-83_-_Detection_Board1.NEG
  GND: SHT3x2.GND, U3.GND, Part2.GND, Part2.ADDR
  N5: SHT3x2.SDA/RH, U3.GPIO21, U3.GPIO3, Part2.SDA
  N6: SHT3x2.SCL/T, U3.GPIO22, Part2.SCL
  N7: U3.GPIO35, J1.pin3
  N8: U3.GPIO32, J2.pin3

custom parts:
  YL-83 Rain Sensor - Control Board: The YL-83 is a rain sensor that has more resistance when dry and less resistance when wet. The module runs at 5V.
  YL-83 Rain Sensor - Detection Board: The YL-83 is a rain sensor that has more resistance when dry and less resistance when wet. The module runs at 5V.
  SHT3x: SHT31 SHT35
  ESP32-38PinWide: Generic 38-Pin ESP32 with wide format (only access to one side of pins on a breadboard) based on Stephen Lilley's HiLetgo ESP-WROOM-32 ESP32 ESP-32S Development Board.
  BH1750: Light Sensor
